# Fritzing sketch MotorControllers (saved by Fritzing 0.9.3b)

parts:
  Part1 = MDD10A
  Pi_Hat = Adafruit 16-Channel PWM + Servo HAT [part_number="Adafruit #2327"]
  Part3 = MDD10A
  Part4 = MDD10A
  12V-Bat = BC9VPC [package=bc9vpc]
  IC1 = Voltage Regulator [package=to-220-alt]
  Raspberry_Pi_1 = Raspberry Pi 3 [part_number=RPI-3-V1.2]
  IC2 = Voltage Regulator [package=to-220-alt]
  U1 = PIC-ICSP [package=molex-1x6]
  U2 = PIC-ICSP [package=molex-1x6]
  U3 = PIC-ICSP [package=molex-1x6]
  U4 = PIC-ICSP [package=molex-1x6]
  M1 = DC Motor
  M2 = DC Motor
  M3 = DC Motor
  M4 = DC Motor
  M5 = DC Motor
  M6 = DC Motor

nets:
  N1: Part1.no_name_yet#connectorBatt-1, U2.GND
  N2: Part1.no_name_yet#connectorBatt-2, U1.GND
  N3: Part1.no_name_yet#connectorM1A-1, M6.pin_1
  N4: Part1.no_name_yet#connectorM1B-1, M6.pin_2
  N5: Part1.no_name_yet#connectorM2A-1, M5.pin_2
  N6: Part1.no_name_yet#connectorM2B-1, M5.pin_1
  N7: Part1.no_name_yet#connectordir-1, Pi_Hat.GPIO4
  N8: Part1.no_name_yet#connectordir-2, Pi_Hat.GPIO17
  GND: Part1.no_name_yet#connectorgnd-1, Pi_Hat.GND, Pi_Hat.GPIO22, Pi_Hat.GPIO23, Part3.no_name_yet#connectorgnd-1, Part4.no_name_yet#connectordir-1, Part4.no_name_yet#connectordir-2, Part4.no_name_yet#connectorgnd-1, Raspberry_Pi_1.GPIO27, Raspberry_Pi_1.GPIO22, Raspberry_Pi_1.GND, Raspberry_Pi_1.GPIO23, U4.PGD
  N9: Part1.no_name_yet#connectorpwm-1, Pi_Hat.#0
  N10: Part1.no_name_yet#connectorpwm-2, Pi_Hat.#1
  N11: Pi_Hat.PWRIN, IC2.OUT
  N12: Pi_Hat.GPIO18, Part3.no_name_yet#connectordir-1
  N13: Pi_Hat.GPIO27, Part3.no_name_yet#connectordir-2
  N14: Pi_Hat.#5, Part4.no_name_yet#connectorpwm-2
  N15: Pi_Hat.#4, Part4.no_name_yet#connectorpwm-1
  N16: Pi_Hat.#3, Part3.no_name_yet#connectorpwm-2
  N17: Pi_Hat.#2, Part3.no_name_yet#connectorpwm-1
  N18: Pi_Hat.5.0V, IC1.OUT
  3V3: Pi_Hat.3.3V, Raspberry_Pi_1.3v3, Raspberry_Pi_1.3V3
  N19: Pi_Hat.GPIO24, Raspberry_Pi_1.GPIO24
  N20: Pi_Hat.SPI_MOSI, Raspberry_Pi_1.GPIO10
  N21: Pi_Hat.SPI_MISO, Raspberry_Pi_1.GPIO9
  N22: Pi_Hat.GPIO25, Raspberry_Pi_1.GPIO25
  N23: Pi_Hat.SPI_SCLK, Raspberry_Pi_1.GPIO11
  N24: Pi_Hat.SPI_CE0, Raspberry_Pi_1.GPIO8
  N25: Pi_Hat.SPI_CE1, Raspberry_Pi_1.GPIO7
  N26: Pi_Hat.EEDATA, Raspberry_Pi_1.ID_SD
  N27: Pi_Hat.EECLK, Raspberry_Pi_1.ID_SC
  N28: Pi_Hat.GPIO5, Raspberry_Pi_1.GPIO5
  N29: Pi_Hat.GPIO6, Raspberry_Pi_1.GPIO6
  N30: Pi_Hat.GPIO12, Raspberry_Pi_1.GPIO12
  N31: Pi_Hat.GPIO13, Raspberry_Pi_1.GPIO13
  N32: Pi_Hat.GPIO19, Raspberry_Pi_1.GPIO19
  N33: Pi_Hat.GPIO16, Raspberry_Pi_1.GPIO16
  N34: Pi_Hat.GPIO26, Raspberry_Pi_1.GPIO26
  N35: Pi_Hat.GPIO20, Raspberry_Pi_1.GPIO20
  N36: Pi_Hat.GPIO21, Raspberry_Pi_1.GPIO21
  N37: Part3.no_name_yet#connectorBatt-1, U2.VCC
  N38: Part3.no_name_yet#connectorBatt-2, U1.VCC
  N39: Part3.no_name_yet#connectorM1A-1, M3.pin_1
  N40: Part3.no_name_yet#connectorM1B-1, M3.pin_2
  N41: Part3.no_name_yet#connectorM2A-1, M4.pin_2
  N42: Part3.no_name_yet#connectorM2B-1, M4.pin_1
  N43: Part4.no_name_yet#connectorBatt-1, U3.PGC
  N44: Part4.no_name_yet#connectorBatt-2, U4.PGC
  N45: Part4.no_name_yet#connectorM1A-1, M2.pin_1
  N46: Part4.no_name_yet#connectorM1B-1, M2.pin_2
  N47: Part4.no_name_yet#connectorM2A-1, M1.pin_2
  N48: Part4.no_name_yet#connectorM2B-1, M1.pin_1
  N49: 12V-Bat.V+, U2.PGM
  N50: 12V-Bat.V-, U1.PGM
  N51: IC1.GND, U1.PGD
  N52: IC1.IN, U2.PGD
  N53: IC2.GND, U1.PGC
  N54: IC2.IN, U2.PGC
  N55: U1.VPP, U4.PGM
  N56: U2.VPP, U3.PGM

custom parts:
  Adafruit 16-Channel PWM + Servo HAT: The Raspberry Pi is a wonderful little computer, but one thing it isn't very good at is controlling DC Servo Motors - these motors need very specific and repetitive timing pulses to set the position. Instead of asking the Pi Linux kernel to send these signals, pop on this handy HAT! It adds the capability to control 16 Servos with perfect timing. It can also do PWM up to 1.6 KHz with 12 bit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
